// Logisim project ProyectoFinal v1.circ as structural Verilog: 11 circuits, main circuit main
module main (
);

  wire CLK, COL, CYCLES, DER, IZQ, RESET;
  wire [3:0] D1, D2, LOSE, WIN;
  wire [6:0] keyboard_1_data;
  wire [7:0] PTS;
  wire [15:0] DEC, PJ, shift_register_1_q0, shift_register_1_q1, shift_register_1_q2, shift_register_1_q3,
       shift_register_1_q4, shift_register_1_q5, shift_register_1_q6, shift_register_1_q7,
       shift_register_1_q8, shift_register_1_q9, shift_register_1_q10, shift_register_1_q11,
       shift_register_1_q12, shift_register_1_q13, shift_register_2_q0, shift_register_2_q1,
       shift_register_2_q2, shift_register_2_q3, shift_register_2_q4, shift_register_2_q5,
       shift_register_2_q6, shift_register_2_q7, shift_register_2_q8, shift_register_2_q9,
       shift_register_2_q10, shift_register_2_q11, shift_register_2_q12, SUM, ULT;

  Clock clock_1 (.out(CYCLES));
  Shift_Register #(.width(16), .length(14)) shift_register_1 (
    .in(SUM), .clk(CLK), .clr(RESET), .q0(shift_register_1_q0), .q1(shift_register_1_q1),
    .q2(shift_register_1_q2), .q3(shift_register_1_q3), .q4(shift_register_1_q4), .q5(shift_register_1_q5),
    .q6(shift_register_1_q6), .q7(shift_register_1_q7), .q8(shift_register_1_q8), .q9(shift_register_1_q9),
    .q10(shift_register_1_q10), .q11(shift_register_1_q11), .q12(shift_register_1_q12),
    .q13(shift_register_1_q13));  // open: shift, out, load, d0, d1, d2, d3, d4, d5, d6, d7, d8, d9, d10, d11, d12, d13
  Reloj reloj_1 (.CYCLES(CYCLES), .WIN(WIN), .LOSE(LOSE), .CLK(CLK));
  Generar_obstaculo generar_obstaculo_1 (.CLK(CLK), .RESET(RESET), .PTS(PTS), .DEC(DEC));
  Suma suma_1 (.DEC(DEC), .SUM(SUM));
  \Colisión  \colisión_1  (.ULT(ULT), .PJ(PJ), .COL(COL));
  Victoria victoria_1 (.PTS(PTS), .WIN(WIN));
  Lose lose_1 (.COL(COL), .LOSE(LOSE));
  Shift_Register #(.width(16), .length(14)) shift_register_2 (
    .in(SUM), .clk(CLK), .clr(RESET), .q0(shift_register_2_q0), .q1(shift_register_2_q1),
    .q2(shift_register_2_q2), .q3(shift_register_2_q3), .q4(shift_register_2_q4), .q5(shift_register_2_q5),
    .q6(shift_register_2_q6), .q7(shift_register_2_q7), .q8(shift_register_2_q8), .q9(shift_register_2_q9),
    .q10(shift_register_2_q10), .q11(shift_register_2_q11), .q12(shift_register_2_q12), .q13(ULT));  // open: shift, out, load, d0, d1, d2, d3, d4, d5, d6, d7, d8, d9, d10, d11, d12, d13
  Update_PJ update_pj_1 (.PJ(PJ), .RESET(RESET), .CLK(CLK), .IZQ(IZQ), .DER(DER), .P0(16'h380));
  Contador_puntos contador_puntos_1 (
    .CLK(CLK), .RESET(RESET), .PTS(PTS), .Display_izq(D1), .Display_der(D2), .Puntos(PTS));
  DotMatrix #(.inputtype("row"), .matrixcols(16), .matrixrows(28)) dotmatrix_1 (
    .row0(shift_register_1_q0), .row1(shift_register_2_q0), .row2(shift_register_1_q1),
    .row3(shift_register_2_q1), .row4(shift_register_1_q2), .row5(shift_register_2_q2),
    .row6(shift_register_1_q3), .row7(shift_register_2_q3), .row8(shift_register_1_q4),
    .row9(shift_register_2_q4), .row10(shift_register_1_q5), .row11(shift_register_2_q5),
    .row12(shift_register_1_q6), .row13(shift_register_2_q6), .row14(shift_register_1_q7),
    .row15(shift_register_2_q7), .row16(shift_register_1_q8), .row17(shift_register_2_q8),
    .row18(shift_register_1_q9), .row19(shift_register_2_q9), .row20(shift_register_1_q10),
    .row21(shift_register_2_q10), .row22(shift_register_1_q11), .row23(shift_register_2_q11),
    .row24(shift_register_1_q12), .row25(shift_register_2_q12), .row26(shift_register_1_q13), .row27(ULT));
  DotMatrix #(.inputtype("row"), .matrixcols(16), .matrixrows(4)) dotmatrix_2 (
    .row0(PJ), .row1(PJ), .row2(PJ), .row3(PJ));
  Keyboard #(.buflen(1)) keyboard_1 (.clk(CLK), .clr(RESET), .data(keyboard_1_data));  // open: re, avail
  Hex_Digit_Display hex_digit_display_1 (.value(D2));  // open: dp
  Hex_Digit_Display hex_digit_display_2 (.value(D1));  // open: dp
  Button button_1 (.out(RESET));
  Hex_Digit_Display hex_digit_display_3 (.value(WIN));  // open: dp
  Hex_Digit_Display hex_digit_display_4 (.value(LOSE));  // open: dp
  Traduccion_Teclado traduccion_teclado_1 (.ASCII(keyboard_1_data), .IZQ(IZQ), .DER(DER));

  // Notes on the sheet:
  //   Puntos
  //   KEYBOARD
  //   G si ganó
  //   F si perdió
endmodule

// GO
module Generar_obstaculo (
  input  CLK,
  input  RESET,
  input  [7:0] PTS,
  output [15:0] DEC
);

  wire and_1_out, and_2_out, and_3_out, and_4_out, comparator_1_eq, comparator_2_gt, comparator_3_eq,
       comparator_4_gt, comparator_5_eq, comparator_6_gt, comparator_7_eq, comparator_8_gt, comparator_9_eq,
       decoder_1_out14, decoder_1_out15, or_2_out;
  wire [3:0] C, random_1_out;

  Counter #(.width(4), .max('hd)) counter_1 (.Q(C), .clk(CLK), .clr(RESET));  // open: load, D, count, carry
  Decoder #(.select(4), .disabled(0)) decoder_1 (
    .out0(DEC[0]), .out1(DEC[1]), .out2(DEC[2]), .out3(DEC[3]), .out4(DEC[4]), .out5(DEC[5]), .out6(DEC[6]),
    .out7(DEC[7]), .out8(DEC[8]), .out9(DEC[9]), .out10(DEC[10]), .out11(DEC[11]), .out12(DEC[12]),
    .out13(DEC[13]), .out14(decoder_1_out14), .out15(decoder_1_out15), .sel(random_1_out), .en(or_2_out));
  Random #(.width(4), .seed(2)) random_1 (.clk(CLK), .out(random_1_out), .clr(RESET));  // open: next
  Comparator #(.width(4)) comparator_1 (.a(C), .b(4'b0000), .eq(comparator_1_eq));  // open: gt, lt
  Comparator comparator_2 (.a(PTS), .b(8'h9), .gt(comparator_2_gt));  // open: eq, lt
  Comparator #(.width(4)) comparator_3 (.a(C), .b(4'b0001), .eq(comparator_3_eq));  // open: gt, lt
  Comparator comparator_4 (.a(PTS), .b(8'h13), .gt(comparator_4_gt));  // open: eq, lt
  Comparator #(.width(4)) comparator_5 (.a(C), .b(4'b0010), .eq(comparator_5_eq));  // open: gt, lt
  or or_1 (DEC[14], decoder_1_out14, decoder_1_out15);
  or or_2 (or_2_out, comparator_1_eq, and_1_out, and_2_out, and_4_out, and_3_out);
  and and_1 (and_1_out, comparator_2_gt, comparator_3_eq);
  and and_2 (and_2_out, comparator_4_gt, comparator_5_eq);
  Comparator comparator_6 (.a(PTS), .b(8'h1d), .gt(comparator_6_gt));  // open: eq, lt
  Comparator #(.width(4)) comparator_7 (.a(C), .b(4'b0011), .eq(comparator_7_eq));  // open: gt, lt
  Comparator comparator_8 (.a(PTS), .b(8'h27), .gt(comparator_8_gt));  // open: eq, lt
  Comparator #(.width(4)) comparator_9 (.a(C), .b(4'b0100), .eq(comparator_9_eq));  // open: gt, lt
  and and_3 (and_3_out, comparator_6_gt, comparator_7_eq);
  and and_4 (and_4_out, comparator_8_gt, comparator_9_eq);

  assign DEC[15] = 1'b0;
endmodule

// S
module Suma (
  input  [15:0] DEC,
  output [15:0] SUM
);

  wire [15:0] adder_1_out;

  Adder #(.width(16)) adder_1 (.a(DEC), .b(DEC), .out(adder_1_out));  // open: cin, cout
  Adder #(.width(16)) adder_2 (.a(DEC), .b(adder_1_out), .out(SUM));  // open: cin, cout
endmodule

// TT
module Traduccion_Teclado (
  input  [6:0] ASCII,
  output IZQ,
  output DER
);

  wire comparator_1_eq, comparator_2_eq, comparator_3_eq, comparator_4_eq;

  Comparator #(.width(7)) comparator_1 (.a(ASCII), .b(7'b1100001), .eq(comparator_1_eq));  // open: gt, lt
  Comparator #(.width(7)) comparator_2 (.a(ASCII), .b(7'b1000001), .eq(comparator_2_eq));  // open: gt, lt
  Comparator #(.width(7)) comparator_3 (.a(ASCII), .b(7'b1100100), .eq(comparator_3_eq));  // open: gt, lt
  Comparator #(.width(7)) comparator_4 (.a(ASCII), .b(7'b1000100), .eq(comparator_4_eq));  // open: gt, lt
  or or_1 (IZQ, comparator_1_eq, comparator_2_eq);
  or or_2 (DER, comparator_3_eq, comparator_4_eq);
endmodule

// M
module Movimiento (
  input  IZQ,
  input  DER,
  input  [15:0] Posicion,
  output [15:0] Updated_X
);

  wire and_1_out, and_2_out, and_3_out, and_4_out, and_5_out, comparator_4_eq, comparator_5_eq, TP_DER1,
       TP_DER2, TP_DER3, TP_IZQ1, TP_IZQ2, TP_IZQ3;
  wire [3:0] bit_extender_1_out, bit_extender_2_out;
  wire [15:0] Shift_DER, Shift_IZQ;

  assign bit_extender_1_out = {{3{1'b0}}, IZQ};  // Bit_Extender bit_extender_1
  assign bit_extender_2_out = {{3{1'b0}}, DER};  // Bit_Extender bit_extender_2
  Multiplexer #(.width(16)) multiplexer_1 (
    .in0(16'hc001), .in1(16'hc001), .out(Updated_X), .sel(TP_IZQ2), .en(TP_IZQ2));
  Multiplexer #(.width(16)) multiplexer_2 (
    .in0(16'he000), .in1(16'he000), .out(Updated_X), .sel(TP_IZQ3), .en(TP_IZQ3));
  and and_1 (and_1_out, IZQ, and_2_out);
  Shifter #(.width(16)) shifter_1 (.in(Posicion), .\dist (bit_extender_1_out), .out(Shift_IZQ));
  Shifter #(.width(16), .shift("lr")) shifter_2 (.in(Posicion), .\dist (bit_extender_2_out), .out(Shift_DER));
  Comparator #(.width(16)) comparator_1 (.a(16'h3), .b(Shift_DER), .eq(TP_IZQ1));  // open: gt, lt
  Multiplexer #(.width(16)) multiplexer_3 (
    .in0(16'h8003), .in1(16'h8003), .out(Updated_X), .sel(TP_IZQ1), .en(TP_IZQ1));
  Comparator #(.width(16)) comparator_2 (.a(16'h4001), .b(Shift_DER), .eq(TP_IZQ2));  // open: gt, lt
  Comparator #(.width(16)) comparator_3 (.a(16'h6000), .b(Shift_DER), .eq(TP_IZQ3));  // open: gt, lt
  Multiplexer #(.width(16)) multiplexer_4 (
    .in0(Shift_IZQ), .in1(Shift_IZQ), .out(Updated_X), .sel(and_1_out), .en(and_1_out));
  and and_2 (and_2_out, ~TP_DER1, ~TP_DER2, ~TP_DER3);  // AND_Gate
  Comparator #(.width(16)) comparator_4 (.a(Posicion), .b(Shift_IZQ), .eq(comparator_4_eq));  // open: gt, lt
  Comparator #(.width(16)) comparator_5 (.a(Posicion), .b(Shift_DER), .eq(comparator_5_eq));  // open: gt, lt
  Multiplexer #(.width(16)) multiplexer_5 (
    .in0(16'hc001), .in1(16'hc001), .out(Updated_X), .sel(TP_DER1), .en(TP_DER1));
  Multiplexer #(.width(16)) multiplexer_6 (
    .in0(16'h8003), .in1(16'h8003), .out(Updated_X), .sel(TP_DER2), .en(TP_DER2));
  Comparator #(.width(16)) comparator_6 (.a(16'h6), .b(Shift_IZQ), .eq(TP_DER3));  // open: gt, lt
  Multiplexer #(.width(16)) multiplexer_7 (.in0(16'h7), .in1(16'h7), .out(Updated_X), .sel(TP_DER3), .en(TP_DER3));
  Multiplexer #(.width(16)) multiplexer_8 (
    .in0(Shift_DER), .in1(Shift_DER), .out(Updated_X), .sel(and_3_out), .en(and_3_out));
  and and_3 (and_3_out, DER, and_5_out);
  and and_4 (and_4_out, comparator_4_eq, comparator_5_eq);
  Multiplexer #(.width(16)) multiplexer_9 (
    .in0(Posicion), .in1(Posicion), .out(Updated_X), .sel(and_4_out), .en(and_4_out));
  Comparator #(.width(16)) comparator_7 (.a(16'hc000), .b(Shift_IZQ), .eq(TP_DER1));  // open: gt, lt
  Comparator #(.width(16)) comparator_8 (.a(16'h8002), .b(Shift_IZQ), .eq(TP_DER2));  // open: gt, lt
  and and_5 (and_5_out, ~TP_IZQ1, ~TP_IZQ2, ~TP_IZQ3);  // AND_Gate

  // Notes on the sheet:
  //   Input
  //   Corrimiento de posición
  //   Para teletransportar a la IZQ primera posición
  //   Para teletransportar a la IZQ segunda posición
  //   Para teletransportar a la IZQ tercera posición
  //   Procedimiento cuando no hay teletransportación y hay corrimiento
  //   Output
  //   Procedimiento si no hay que hacer corrimiento
  //   Para teletransportar a la DER primera posición
  //   Para teletransportar a la DER segunda posición
  //   Para teletransportar a la DER tercera posición
endmodule

// UPJ
module Update_PJ (
  input  CLK,
  input  IZQ,
  input  DER,
  input  [15:0] P0,
  input  RESET,
  output [15:0] PJ
);

  wire counter_1_q;
  wire [15:0] multiplexer_1_out, register_1_q, X;

  Register #(.width(16)) register_1 (.D(X), .Q(register_1_q), .clk(CLK), .clr(RESET));  // open: en
  Multiplexer #(.width(16), .enable("false")) multiplexer_1 (
    .in0(P0), .in1(register_1_q), .out(multiplexer_1_out), .sel(counter_1_q));
  Movimiento movimiento_1 (.IZQ(IZQ), .DER(DER), .Posicion(multiplexer_1_out), .Updated_X(PJ));
  Counter #(.width(1), .max('h1), .ongoal("stay")) counter_1 (
    .Q(counter_1_q), .clk(CLK), .clr(RESET));  // open: load, D, count, carry
  Multiplexer #(.width(16), .enable("false")) multiplexer_2 (.in0(P0), .in1(PJ), .out(X), .sel(counter_1_q));
endmodule

// CP
module Contador_puntos (
  input  CLK,
  input  RESET,
  input  [7:0] PTS,
  output [7:0] Puntos,
  output [3:0] Display_izq,
  output [3:0] Display_der
);

  wire and_1_out, and_2_out, and_3_out, and_4_out, comparator_1_gt, comparator_2_eq, comparator_3_gt,
       comparator_4_eq, comparator_5_eq, comparator_6_gt, comparator_7_eq, comparator_8_gt, comparator_9_eq,
       or_1_out;
  wire [7:0] C;
  wire [7:4] divider_1_out, divider_1_rem;

  Counter #(.max('hf), .ongoal("load")) counter_1 (
    .D(8'h2), .Q(C), .clk(CLK), .clr(RESET));  // open: load, count, carry
  Comparator comparator_1 (.a(PTS), .b(8'h9), .gt(comparator_1_gt));  // open: eq, lt
  Comparator comparator_2 (.a(C), .b(8'h3), .eq(comparator_2_eq));  // open: gt, lt
  Comparator comparator_3 (.a(PTS), .b(8'h13), .gt(comparator_3_gt));  // open: eq, lt
  Comparator comparator_4 (.a(C), .b(8'h5), .eq(comparator_4_eq));  // open: gt, lt
  Comparator comparator_5 (.a(C), .b(8'hf), .eq(comparator_5_eq));  // open: gt, lt
  or or_1 (or_1_out, comparator_5_eq, and_1_out, and_2_out, and_4_out, and_3_out);
  and and_1 (and_1_out, comparator_1_gt, comparator_2_eq);
  and and_2 (and_2_out, comparator_3_gt, comparator_4_eq);
  Counter #(.max('h32)) counter_2 (.Q(Puntos), .clk(or_1_out), .clr(RESET));  // open: load, D, count, carry
  Divider divider_1 (
    .a(Puntos), .b(8'ha), .out({divider_1_out, Display_izq}), .rem({divider_1_rem, Display_der}));  // open: upper
  Comparator comparator_6 (.a(PTS), .b(8'h1d), .gt(comparator_6_gt));  // open: eq, lt
  Comparator comparator_7 (.a(C), .b(8'h7), .eq(comparator_7_eq));  // open: gt, lt
  Comparator comparator_8 (.a(PTS), .b(8'h27), .gt(comparator_8_gt));  // open: eq, lt
  Comparator comparator_9 (.a(C), .b(8'h9), .eq(comparator_9_eq));  // open: gt, lt
  and and_3 (and_3_out, comparator_6_gt, comparator_7_eq);
  and and_4 (and_4_out, comparator_8_gt, comparator_9_eq);
endmodule

// V
module Victoria (
  input  [7:0] PTS,
  output [3:0] WIN
);

  wire comparator_1_eq;

  Comparator comparator_1 (.a(PTS), .b(8'h32), .eq(comparator_1_eq));  // open: gt, lt
  Multiplexer #(.width(4), .disabled(0)) multiplexer_1 (
    .in0(4'b0110), .in1(4'b0110), .out(WIN), .sel(comparator_1_eq), .en(comparator_1_eq));
endmodule

// CLK
module Reloj (
  input  CYCLES,
  input  [3:0] WIN,
  input  [3:0] LOSE,
  output CLK
);

  wire bitfinder_1_found, bitfinder_2_found, or_1_out;

  Multiplexer #(.enable("false")) multiplexer_1 (.in0(CYCLES), .in1(1'b0), .out(CLK), .sel(or_1_out));
  or or_1 (or_1_out, bitfinder_1_found, bitfinder_2_found);
  BitFinder #(.width(4)) bitfinder_1 (.in(WIN), .found(bitfinder_1_found));  // open: index
  BitFinder #(.width(4)) bitfinder_2 (.in(LOSE), .found(bitfinder_2_found));  // open: index
endmodule

// COL
module \Colisión  (
  input  [15:0] ULT,
  input  [15:0] PJ,
  output COL
);

  wire and_1_out, and_2_out, and_3_out, and_4_out, and_5_out, and_6_out, and_7_out, and_8_out, and_9_out,
       and_10_out, and_11_out, and_12_out, and_13_out, and_14_out, and_15_out, and_16_out;

  and and_1 (and_1_out, ULT[0], PJ[0]);
  and and_2 (and_2_out, ULT[1], PJ[1]);
  and and_3 (and_3_out, ULT[2], PJ[2]);
  and and_4 (and_4_out, ULT[3], PJ[3]);
  and and_5 (and_5_out, ULT[4], PJ[4]);
  and and_6 (and_6_out, ULT[5], PJ[5]);
  and and_7 (and_7_out, ULT[6], PJ[6]);
  and and_8 (and_8_out, ULT[7], PJ[7]);
  and and_9 (and_9_out, ULT[8], PJ[8]);
  and and_10 (and_10_out, ULT[9], PJ[9]);
  and and_11 (and_11_out, ULT[10], PJ[10]);
  and and_12 (and_12_out, ULT[11], PJ[11]);
  and and_13 (and_13_out, ULT[12], PJ[12]);
  and and_14 (and_14_out, ULT[13], PJ[13]);
  and and_15 (and_15_out, ULT[14], PJ[14]);
  and and_16 (and_16_out, ULT[15], PJ[15]);
  or or_1 (COL, and_1_out, and_2_out, and_3_out, and_4_out, and_5_out, and_6_out, and_7_out, and_8_out, and_9_out, and_10_out, and_11_out, and_12_out, and_13_out, and_14_out, and_15_out, and_16_out);

  // Other names for the same wires on the sheet: O1 = PJ[0]; O2 = PJ[1]; O3 = PJ[2]; O4 = PJ[3]; O5 = PJ[4];
  //   O6 = PJ[5]; O7 = PJ[6]; O8 = PJ[7]; O9 = PJ[8]; O10 = PJ[9]; O11 = PJ[10]; O12 = PJ[11]; O13 = PJ[12];
  //   O14 = PJ[13]; O15 = PJ[14]; O16 = PJ[15]; U1 = ULT[0]; U2 = ULT[1]; U3 = ULT[2]; U4 = ULT[3]; U5 = ULT[4];
  //   U6 = ULT[5]; U7 = ULT[6]; U8 = ULT[7]; U9 = ULT[8]; U10 = ULT[9]; U11 = ULT[10]; U12 = ULT[11]; U13 = ULT[12];
  //   U14 = ULT[13]; U15 = ULT[14]; U16 = ULT[15]
endmodule

// L
module Lose (
  input  COL,
  output [3:0] LOSE
);

  Multiplexer #(.width(4), .disabled(0)) multiplexer_1 (.in0(4'b1111), .in1(4'b1111), .out(LOSE), .sel(COL), .en(COL));
endmodule
